# Fritzing sketch EnvironmentEthernetMonitor (saved by Fritzing 0.8.7b)
breadboards: 1

parts:
  Part1 = Arduino Board Ethernet  # not connected
  PIR1 = PIR sensor
  Part2 = Arduino ProtoShield
  DHT1 = DHT11 Humitidy and Temperature Sensor
  R1 = Resistor [package="2512 [SMD]"]  # not connected
  R1_2 = Resistor [tolerance=±5% resistance=220 package=THT]  # not connected
  R1_3 = Resistor [tolerance=±5% resistance=4.7 package=THT]
  DS1 = DS18B20 1-Wire Temperature Sensor [part_number=DS18B20]
  DS2 = DS18B20 1-Wire Temperature Sensor [part_number=DS18B20]
  R3 = Resistor [tolerance=±5% resistance=4.7 package=THT]
  Part3 = Barometric Pressure Sensor - BMP085 Breakout
  Part4 = Digital Temperature Sensor Breakout - TMP102
  HS1101 = Variable Capacitor [capacitance=100nF max_capacitance=10pF min_capacitance=2pF voltage=35V]
  R4 = Resistor [package="2010 [SMD]"]
  R5 = Resistor [tolerance=±5% resistance=10M package=THT]
  Parallax_27972_and_MG811_Sensor = Header 5 [package=1x05-1mm]
  Parallax_27972_Breakout = Header 5 [package=1x05-1mm]

nets:
  VDD: PIR1.VDD, Part2.5V, DHT1.VDD, R1_3.Pin_0, DS1.VDD, DS2.VDD, R3.Pin_0, Part3.VCC, Part4.V+, HS1101.1, R4.Pin_1, R5.Pin_0, Parallax_27972_and_MG811_Sensor.1, Parallax_27972_and_MG811_Sensor.3, Parallax_27972_Breakout.3
  N1: PIR1.SIG, Part2.D2
  GND: PIR1.GND, Part2.GND, DHT1.GND, DS1.GND, DS2.GND, Part3.GND, Part3.EOC, Part3.XCLR, Part4.GND, Part4.ALERT, Part4.ADD0, Parallax_27972_and_MG811_Sensor.4, Parallax_27972_Breakout.4
  N2: Part2.D3, Parallax_27972_Breakout.1
  N3: Part2.D4, R4.Pin_0
  N4: Part2.D5, DS1.DQ, DS2.DQ, R3.Pin_1
  N5: Part2.A5, Part3.SCL, Part4.SCL
  N6: Part2.A4, Part3.SDA, Part4.SDA
  N7: Part2.A3, Parallax_27972_Breakout.2
  N8: Part2.A1, Parallax_27972_Breakout.5
  N9: Part2.A0, Parallax_27972_and_MG811_Sensor.5
  N10: DHT1.DATA, R1_3.Pin_1
  N11: HS1101.0, R5.Pin_1

custom parts:
  DHT11 Humitidy and Temperature Sensor: DHT11 Humidity and Temperature Sensor
