# Fritzing sketch Schematic Example (saved by Fritzing 0.8.7b)
breadboards: 1

parts:
  4n25 = IC, DIP package, 6 pins [chip_label=IC]
  R1 = Resistor [tolerance=±5% resistance=390 package=THT]
  D1 = Rectifier Diode [part_number=1N4001 package="300 mil [THT]"]
  D2 = Zener Diode [part_number=1N4732A breakdown_voltage=5.1V package="Melf DO-213 AB [SMD]"]
  C1 = Ceramic Capacitor [capacitance=100nF package="100 mil [THT, multilayer]"]
  C2 = Ceramic Capacitor [capacitance=100nF package="100 mil [THT, multilayer]"]
  R2 = Resistor [tolerance=±5% resistance=4.7k package=THT]
  Arduino = Arduino Uno (Rev3)

nets:
  N1: 4n25.pin1, D2.anode, C1.1
  GND: 4n25.pin2, C1.0
  N2: 4n25.pin4, C2.1, Arduino.GND
  N3: 4n25.pin5, C2.0, R2.Pin_0
  N4: R1.Pin_0, D1.cathode
  N5: R1.Pin_1, D2.cathode
  0V: D1.anode
  N6: R2.Pin_1, Arduino.D2, Arduino.D3_PWM

notes:
  Coil - Terminal
  Vehicle Ground
  Connect R2 to two seperate interupt pins on the arduino
  Connect pin 1 of the IC to the negative terminal of the coil via the voltage limiting circuit.
  Connect pin 2 of the IC to the vehicle ground.
